# Fritzing sketch schematics_plane (saved by Fritzing 1.0.7)
breadboards: 2

parts:
  Part1 = Arduino Nano (Rev3.0)
  U1 = TRANSISTOR_NPN_2 [package=to-92]
  R1 = Resistor [tolerance=±5% resistance=220 package="1206 [SMD]"]
  R2 = Resistor [tolerance=±5% resistance=220 package="1206 [SMD]"]
  SBUS_Empfänger = Dagu DGServo 9g header (male) [package=THT]
  Part2 = I2C level shifter bidirectional
  Lora32 = Heltec WiFi Kit 32 V3 [part_number=HTIT-WB32_V3]
  GPS_Modul = GT-U8-GPS module
  Part4 = HMC5883L Triple-axis Magnetometer [part_number=1746]
  BMP280 = Barometric Pressure Sensor - BMP180 Breakout (GY-68)
  Part3 = InvenSense MPU6050

nets:
  N1: Part1.D0/RX, U1.E, R1.Pin_0
  GND: Part1.GND, U1.C, SBUS_Empfänger.gnd, Part2.GND, Lora32.pin_18, Lora32.pin_19, GPS_Modul.Pin_2, Part4.GND, BMP280.GND, Part3.GND
  5V: Part1.5V, R1.Pin_1, SBUS_Empfänger.Vcc, Part2.HV, Lora32.pin_20
  N2: Part1.A5, Part2.HV4
  N3: Part1.A4, Part2.HV3
  N4: U1.B, R2.Pin_1
  N5: R2.Pin_0, SBUS_Empfänger.pulse
  N6: Part2.LV4, Lora32.pin_32, Part4.SCL, BMP280.SCL, Part3.SCL
  N7: Part2.LV3, Lora32.pin_31, Part4.SDA, BMP280.SDA, Part3.SDA
  VCC: Part2.LV, Lora32.pin_16, Lora32.pin_17, GPS_Modul.Pin_1, Part4.VIN, BMP280.VCC, Part3.VCC
  N8: Lora32.pin_6, GPS_Modul.Pin_3
  N9: Lora32.pin_21, Lora32.pin_22

custom parts:
  Heltec WiFi Kit 32 V3: The Heltec WiFi Kit 32 (V3) is an IoT development board designed and produced by Heltec Automation and based on the Espressif ESP32 processor module. The board includes WiFi and Bluetooth/BLE functions, as well as a 0.96″ OLED display and a Li-Po battery management system. Links: Heltec WiFi Kit 32 (V3) product page Github
  GT-U8-GPS module: GPS / BDS W/GT-U8 WITH CERAMIC ANTENNA.
